// Digital circuit downcounter.dig as structural Verilog
module downcounter (
  input  rst,
  input  c1khz,
  input  count,
  input  load,
  input  [3:0] pm10,
  input  [3:0] pm1,
  input  [3:0] ps10,
  input  [3:0] ps1,
  output [3:0] m10,
  output [3:0] m1,
  output [3:0] s10,
  output [3:0] s1,
  output zero
);

  wire not_1_out, or_1_out, or_2_out, or_3_out, or_4_out, or_5_out, or_6_out, or_7_out, or_8_out, or_9_out,
       project_downcounter_new_1_zero, project_downcounter_new_2_zero, project_downcounter_new_3_zero,
       project_downcounter_new_4_zero;
  wire [3:0] multiplexer_1_out, multiplexer_2_out, multiplexer_3_out, multiplexer_4_out;

  not not_1 (not_1_out, rst);
  or or_1 (or_1_out, load, project_downcounter_new_1_zero);
  or or_2 (or_2_out, load, project_downcounter_new_2_zero);
  or or_3 (or_3_out, load, project_downcounter_new_3_zero);
  or or_4 (or_4_out, load, project_downcounter_new_4_zero);
  Multiplexer #(.Bits(4)) multiplexer_1 (.sel(load), .in_0(4'b1001), .in_1(pm10), .out(multiplexer_1_out));
  Multiplexer #(.Bits(4)) multiplexer_2 (.sel(load), .in_0(4'b1001), .in_1(pm1), .out(multiplexer_2_out));
  Multiplexer #(.Bits(4)) multiplexer_3 (.sel(load), .in_0(4'b0101), .in_1(ps10), .out(multiplexer_3_out));
  Multiplexer #(.Bits(4)) multiplexer_4 (.sel(load), .in_0(4'b1001), .in_1(ps1), .out(multiplexer_4_out));
  project_downcounter_new project_downcounter_new_1 (
    .EN(project_downcounter_new_2_zero), .LOAD(or_1_out), .IN(multiplexer_1_out), .CLK(c1khz),
    .RESET(not_1_out), .CNT(m10), .ZERO(project_downcounter_new_1_zero));
  project_downcounter_new project_downcounter_new_2 (
    .EN(project_downcounter_new_3_zero), .LOAD(or_2_out), .IN(multiplexer_2_out), .CLK(c1khz),
    .RESET(not_1_out), .CNT(m1), .ZERO(project_downcounter_new_2_zero));
  project_downcounter_new project_downcounter_new_3 (
    .EN(project_downcounter_new_4_zero), .LOAD(or_3_out), .IN(multiplexer_3_out), .CLK(c1khz),
    .RESET(not_1_out), .CNT(s10), .ZERO(project_downcounter_new_3_zero));
  project_downcounter_new project_downcounter_new_4 (
    .EN(count), .LOAD(or_4_out), .IN(multiplexer_4_out), .CLK(c1khz), .RESET(not_1_out), .CNT(s1),
    .ZERO(project_downcounter_new_4_zero));
  or or_5 (or_5_out, m10[0], m10[1], m10[2], m10[3]);
  or or_6 (or_6_out, m1[0], m1[1], m1[2], m1[3]);
  or or_7 (or_7_out, s10[0], s10[1], s10[2], s10[3]);
  or or_8 (or_8_out, s1[0], s1[1], s1[2], s1[3]);
  or or_9 (or_9_out, or_5_out, or_6_out, or_7_out, or_8_out);
  not not_2 (zero, or_9_out);
endmodule
