// Digital circuit eggimer.dig as structural Verilog
module eggimer (
  input  _1_kHz
);

  wire downcounter_1_zero, PRESET_out, RST_out, START_out, u_controller_countdown, u_controller_load,
       u_controller_start, u_counter_endd;
  wire [3:0] dipswitch_1_out, dipswitch_5_out, dipswitch_9_out, dipswitch_13_out, downcounter_1_m1,
       downcounter_1_m10, downcounter_1_s1, downcounter_1_s10;

  Button #(.activeLow("true")) RST (.out(RST_out));
  Seven_Seg_Hex seven_seg_hex_1 (.d(downcounter_1_m10), .dp(1'b0));
  DipSwitch dipswitch_1 (.out(dipswitch_1_out[3]));
  DipSwitch dipswitch_2 (.out(dipswitch_1_out[2]));
  DipSwitch dipswitch_3 (.out(dipswitch_1_out[1]));
  Seven_Seg_Hex seven_seg_hex_2 (.d(downcounter_1_m1), .dp(1'b1));
  downcounter downcounter_1 (
    .rst(RST_out), .c1khz(_1_kHz), .count(u_controller_countdown), .load(u_controller_load),
    .pm10(dipswitch_1_out), .pm1(dipswitch_5_out), .ps10(dipswitch_9_out), .ps1(dipswitch_13_out),
    .m10(downcounter_1_m10), .m1(downcounter_1_m1), .s10(downcounter_1_s10), .s1(downcounter_1_s1),
    .zero(downcounter_1_zero));
  DipSwitch dipswitch_4 (.out(dipswitch_1_out[0]));
  DipSwitch dipswitch_5 (.out(dipswitch_5_out[3]));
  DipSwitch dipswitch_6 (.out(dipswitch_5_out[2]));
  Seven_Seg_Hex seven_seg_hex_3 (.d(downcounter_1_s10), .dp(1'b0));
  DipSwitch dipswitch_7 (.out(dipswitch_5_out[1]));
  DipSwitch dipswitch_8 (.out(dipswitch_5_out[0]));
  DipSwitch dipswitch_9 (.out(dipswitch_9_out[3]));
  Seven_Seg_Hex seven_seg_hex_4 (.d(downcounter_1_s1), .dp(1'b0));
  DipSwitch dipswitch_10 (.out(dipswitch_9_out[2]));
  DipSwitch dipswitch_11 (.out(dipswitch_9_out[1]));
  DipSwitch dipswitch_12 (.out(dipswitch_9_out[0]));
  DipSwitch dipswitch_13 (.out(dipswitch_13_out[3]));
  DipSwitch dipswitch_14 (.out(dipswitch_13_out[2]));
  DipSwitch dipswitch_15 (.out(dipswitch_13_out[1]));
  DipSwitch dipswitch_16 (.out(dipswitch_13_out[0]));
  controller #(.applicationType("IVERILOG")) u_controller (
    .clk(_1_kHz), .rst(RST_out), .beginn(START_out), .reset(PRESET_out), .zero(downcounter_1_zero),
    .endd(u_counter_endd), .load(u_controller_load), .start(u_controller_start),
    .countdown(u_controller_countdown));
  Button START (.out(START_out));
  Button PRESET (.out(PRESET_out));
  counter #(.applicationType("IVERILOG")) u_counter (
    .rst(RST_out), .clk(_1_kHz), .start(u_controller_start), .endd(u_counter_endd));

  // Notes on the sheet:
  //   _1_kHz: Hz: 1000
endmodule

/* Code of controller:
module controller(
    input clk,
    input rst,
    input beginn, 
    input reset,
    input zero,
    input endd,
    output load,
    output start,
    output countdown
    );
    
    // write your code here
    
    reg [1:0] state; //"0" as "PAUSE" state, "1" as "COUNT" state and "2" as "START" state

    assign countdown = (endd && ~start && state != 0);
    assign start = (state == 2 && state != 0);
    assign load = reset;

    always @(posedge clk, negedge rst)
    begin
    	if (~rst) state <= 0;
    	else
        begin 
     	   if(reset) state <= 0;
    	   else
           begin
             if(state == 0)
             begin
           	if(beginn) 
                begin
                	if(~zero) state <= 2;
                        else state <= 0;
                end  
             end
             else 
             begin
                if(endd) 
                begin
                	if(~zero) state <= 2;
                        else state <= 0;
                end  
                else 
                begin
                	if(~zero) state <= 1;
                        else state <= 0;
                end
              end
           end
        end
    end //always

endmodule
*/

/* Code of counter:
module counter(
    input rst,
    input clk,
    input start,
    output endd);
    
    reg [9:0] cnt;
    
    assign endd = (cnt==0);
    
    always @(posedge clk, negedge rst)
    begin
        if (~rst)
        begin
            cnt <= 0;
        end
        else
        begin
            if (start)
                cnt <= 999;
            else if (~endd)
                cnt <= cnt-1;
        end
    end // always
endmodule
*/
